# Fritzing sketch Joystick 6 dc motor (saved by Fritzing 0.9.9b)

parts:
  Part1 = Arduino Mega 2560 (Rev3)
  Part2 = Thumb Joystick
  Part3 = Thumb Joystick
  MD03A1 = Dual VNH2SP30 Motor Driver [part_number=MD03A]
  MD03A2 = Dual VNH2SP30 Motor Driver [part_number=MD03A]
  MD03A3 = Dual VNH2SP30 Motor Driver [part_number=MD03A]
  M1 = DC Motor
  M2 = DC Motor
  M3 = DC Motor
  M4 = DC Motor
  M5 = DC Motor
  M6 = DC Motor
  VCC1 = Battery block 9V
  VCC2 = Battery block 9V
  VCC3 = Battery block 9V

nets (from the schematic view):
  N1: Part1.A0, Part2.HORZ
  N2: Part1.A1, Part2.VERT
  N3: Part1.A2, Part3.HORZ
  N4: Part1.A3, Part3.VERT
  GND: Part1.GND, Part2.GND, Part3.GND, MD03A1.GND#151, MD03A2.GND#151, MD03A3.GND#138, VCC2.-
  N5: Part1.D13_PWM, MD03A1.1DIAG/EN
  N6: Part1.D12_PWM, MD03A1.2DIAG/EN
  N7: Part1.D11_PWM, MD03A2.1DIAG/EN
  N8: Part1.D10_PWM, MD03A2.2DIAG/EN
  N9: Part1.D9_PWM, MD03A3.1DIAG/EN
  N10: Part1.D8_PWM, MD03A3.2DIAG/EN
  VCC: Part1.IOREF, Part2.VCC, Part3.VCC, MD03A2.+5V_(IN)
  N11: Part1.5V, MD03A1.+5V_(IN), MD03A3.+5V_(IN)
  N12: Part1.D2_PWM, MD03A3.2PWM
  N13: Part1.D3_PWM, MD03A3.PWM
  N14: Part1.D4_PWM, MD03A2.2PWM
  N15: Part1.D5_PWM, MD03A2.PWM
  N16: Part1.D6_PWM, MD03A1.2PWM
  N17: Part1.D7_PWM, MD03A1.PWM
  N18: Part1.D22, MD03A1.1INa
  N19: Part1.D23, MD03A1.1INb
  N20: Part1.D24, MD03A1.2INb#142
  N21: Part1.D25, MD03A1.2INb#143
  N22: Part1.D26, MD03A2.1INa
  N23: Part1.D27, MD03A2.1INb
  N24: Part1.D28, MD03A2.2INb#142
  N25: Part1.D29, MD03A2.2INb#143
  N26: Part1.D30, MD03A3.1INa
  N27: Part1.D31, MD03A3.1INb
  N28: Part1.D32, MD03A3.2INb#142
  N29: Part1.D33, MD03A3.2INb#143
  N30: MD03A1.OUT_1A, M1.pin_1
  N31: MD03A1.OUT_1B, M1.pin_2
  N32: MD03A1.OUT_2A, M2.pin_1
  N33: MD03A1.OUT_2B, M2.pin_2
  N34: MD03A1.VIN, VCC3.+
  N35: MD03A2.OUT_1A, M3.pin_1
  N36: MD03A2.OUT_1B, M3.pin_2
  N37: MD03A2.OUT_2A, M4.pin_1
  N38: MD03A2.OUT_2B, M4.pin_2
  N39: MD03A2.VIN, VCC2.+
  N40: MD03A3.OUT_1A, M5.pin_1
  N41: MD03A3.OUT_1B, M5.pin_2
  N42: MD03A3.OUT_2A, M6.pin_1
  N43: MD03A3.OUT_2B, M6.pin_2
  N44: MD03A3.VIN, VCC1.+
  N45: MD03A3.GND#151, VCC1.-

// code stored in the sketch: Joystick 6 dc motor.ino
#define SPEED1 13
#define SPEED2 12
#define SPEED3 11
#define SPEED4 10
#define SPEED5 9
#define SPEED6 8
#define mtr1in1 22
#define mtr1in2 23
#define mtr2in1 24
#define mtr2in2 25
#define mtr3in1 26
#define mtr3in2 27
#define mtr4in1 28
#define mtr4in2 29
#define mtr5in1 30
#define mtr5in2 31
#define mtr6in1 32
#define mtr6in2 33

// add 6 more pins for pwm pin on motor driver that activates the motor ctrl1-6 from D2-D7

int jx1=0;
int jx2=0;
int jy1=0;
int jy2=0;
char x;


void setup() {
  // put your setup code here, to run once:
  for (int i=22; i<34; i=i+1){
    pinMode(i, OUTPUT);
  }
  for (int j=8; j<14; j=j+1){
    pinMode(j, OUTPUT);
  }

  for (int k=2; k<8; k=k+1){
    digitalWrite(k, LOW);
  }
  Serial.begin(9600);

}

void loop() {
  // put your main code here, to run repeatedly:
  
  jx1=analogRead(A0);
  jy1=analogRead(A1);
  jx2=analogRead(A2);
  jy2=analogRead(A3);
  
  jx1=map(jx1, 0, 1023, 0, 255);
  jx2=map(jx2, 0, 1023, 0, 255);
  jy1=map(jy1, 0, 1023, 0, 255);
  jy2=map(jy2, 0, 1023, 0, 255);


  x=Serial.read();
  
  if(x=='1'){

     digitalWrite(7, HIGH);
     digitalWrite(6, HIGH);     // Pins that turn on the motor driver

     digitalWrite(mtr1in1, HIGH);
     digitalWrite(mtr1in2, LOW);
     analogWrite(SPEED1, jx1);
     digitalWrite(mtr2in1, HIGH);
     digitalWrite(mtr2in2, LOW);
     analogWrite(SPEED2, jx2);
    
  }

    if(x=='2'){

     digitalWrite(5, HIGH);
     digitalWrite(4, HIGH);     // Pins that turn on the motor driver

     digitalWrite(mtr3in1, HIGH);
     digitalWrite(mtr3in2, LOW);
     analogWrite(SPEED3, jx1);
     digitalWrite(mtr4in1, HIGH);
     digitalWrite(mtr4in2, LOW);
     analogWrite(SPEED4, jx2);
    
  }

      if(x=='3'){

     digitalWrite(3, HIGH);
     digitalWrite(2, HIGH);     // Pins that turn on the motor driver

     digitalWrite(mtr5in1, HIGH);
     digitalWrite(mtr5in2, LOW);
     analogWrite(SPEED5, jx1);
     digitalWrite(mtr6in1, HIGH);
     digitalWrite(mtr6in2, LOW);
     analogWrite(SPEED6, jx2);
    
  }
}
